# Fritzing sketch self-balaning-bot (saved by Fritzing 0.9.5d)

parts:
  U1 = BATTERY-2 [package=battery-aa]
  U2 = BATTERY-2 [package=battery-aa]
  U3 = BATTERY-2 [package=battery-aa]
  M1 = RioRand LM2596
  M2 = DC Motor  # not connected
  M3 = DC Motor
  U4 = ESP32S-HiLetgo [part_number=ESP32S-HiLetgo]
  M4 = gy9250
  M5 = BTS7960
  M6 = BTS7960

nets:
  N1: U1.-1, M1.Pin_1, M5.pin9, M6.pin9
  N2: U1.+1, U2.-1
  N3: U2.+1, U3.-1
  N4: U3.+1, M1.Pin_2, M5.pin10, M6.pin10
  N5: M1.Pin_3, M5.pin7, M6.pin7
  N6: M1.Pin_4, M5.pin8, M6.pin8
  N7: M3.pin_1, M5.pin11
  N8: U4.3.3, M4.pin1, M4.pin9
  N9: U4.GPIO39, M6.pin1
  N10: U4.GPIO34, M6.pin2
  N11: U4.GPIO35, M6.pin4
  N12: U4.GPIO32, M6.pin3
  N13: U4.GND, M4.pin2, M4.pin7, M4.pin10
  N14: U4.GPIO10, M5.pin1
  N15: U4.GPIO11, M5.pin3
  N16: U4.GPIO0, M5.pin2
  N17: U4.GPIO4, M5.pin4
  N18: U4.GPIO16, M4.pin3
  N19: U4.GPIO17, M4.pin4
  N20: U4.GPIO18, M4.pin8

custom parts:
  ESP32S-HiLetgo: HiLetgo ESP-WROOM-32 ESP32 ESP-32S Development Board 2.4GHz Dual-Mode WiFi + Bluetooth Dual Cores Microcontroller The ESP32 integrated with Antenna switches, RF Balun, power amplifiers, low-noise amplifiers, filters, and management modules, and the entire solution occupies the least area of PCB. 2.4 GHz Wi-Fi plus Bluetooth dual-mode chip, with TSMC Ultra-low power consumption 40nm technology,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
  gy9250: MPU-9250 module (three-axis gyroscope + three-axis acceleration + three-axis magnetic field). The generic model from ebay et. al. rather than the Sparkfun version.
  BTS7960: BTS7960 43A Peak Power H-Bridge PWM Motor Driver
